// Logisim project CPU.circ as structural Verilog: 17 circuits, main circuit main
module main (
  output [7:0] out_1
);

  wire alucpu_1_zero, and_1_out, and_2_out, bcd_to_7_segment_decoder_5_p1, CLK, control_1_alusrc,
       control_1_branch, control_1_jump, control_1_memread, control_1_memtoreg, control_1_memwrite,
       control_1_regdst, control_1_regwrite, multiplexer_2_out, n7_segment_display_1_p1,
       n7_segment_display_1_p2, n7_segment_display_2_p2, n7_segment_display_3_p2, n7_segment_display_5_p2,
       n7_segment_display_5_p3, n7_segment_display_7_p2, n7_segment_display_8_p2, n7_segment_display_8_p3,
       n7_segment_display_10_p3, n7_segment_display_10_p4, n7_segment_display_11_p2, Reiniciar,
       ReiniciarManual, sumador_1_cout;
  wire [1:0] alucontrol_1_c, control_1_aluop0;
  wire [2:0] multiplexer_1_out;
  wire [7:0] alucpu_1_s, archivoderegistros_1_readdata1, archivoderegistros_1_readdata2,
       binary_to_bcd_converter_3_p1, binary_to_bcd_converter_4_p1, binary_to_bcd_converter_5_p1,
       dataMemory_dout, multiplexer_3_out, multiplexer_4_out, multiplexer_5_out, multiplexer_6_out,
       sumador_1_s, sumador_2_s;
  wire [15:0] rom_1_data;

  // _7_Segment_Display 7_segment_display_1: pin names not known; wires that end beside it: n7_segment_display_1_p1, n7_segment_display_1_p2
  // BCD_to_7_Segment_decoder bcd_to_7_segment_decoder_1: pin names not known
  // _7_Segment_Display 7_segment_display_2: pin names not known; wires that end beside it: n7_segment_display_1_p2, n7_segment_display_2_p2
  // BCD_to_7_Segment_decoder bcd_to_7_segment_decoder_2: pin names not known
  // _7_Segment_Display 7_segment_display_3: pin names not known; wires that end beside it: n7_segment_display_2_p2, n7_segment_display_3_p2
  // BCD_to_7_Segment_decoder bcd_to_7_segment_decoder_3: pin names not known
  _7_Segment_Display u_7_segment_display_4 ();  // open: g, f, a, b, e, d, c, dp
  // BCD_to_7_Segment_decoder bcd_to_7_segment_decoder_4: pin names not known
  // Binary_to_BCD_converter #(.binvalue(8)) binary_to_bcd_converter_1: pin names not known; wires that end beside it: out_1
  // _7_Segment_Display 7_segment_display_5: pin names not known; wires that end beside it: n7_segment_display_3_p2, n7_segment_display_5_p2, n7_segment_display_5_p3
  // BCD_to_7_Segment_decoder bcd_to_7_segment_decoder_5: pin names not known; wires that end beside it: bcd_to_7_segment_decoder_5_p1, bcd_to_7_segment_decoder_5_p1
  _7_Segment_Display u_7_segment_display_6 ();  // open: g, f, a, b, e, d, c, dp
  // BCD_to_7_Segment_decoder bcd_to_7_segment_decoder_6: pin names not known
  // _7_Segment_Display 7_segment_display_7: pin names not known; wires that end beside it: n7_segment_display_5_p3, n7_segment_display_7_p2
  // _7_Segment_Display 7_segment_display_8: pin names not known; wires that end beside it: n7_segment_display_7_p2, n7_segment_display_8_p2, n7_segment_display_8_p3
  // BCD_to_7_Segment_decoder bcd_to_7_segment_decoder_7: pin names not known
  // BCD_to_7_Segment_decoder bcd_to_7_segment_decoder_8: pin names not known
  _7_Segment_Display u_7_segment_display_9 ();  // open: g, f, a, b, e, d, c, dp
  // BCD_to_7_Segment_decoder bcd_to_7_segment_decoder_9: pin names not known
  // _7_Segment_Display 7_segment_display_10: pin names not known; wires that end beside it: n7_segment_display_8_p2, n7_segment_display_8_p3, n7_segment_display_10_p3, n7_segment_display_10_p4
  // BCD_to_7_Segment_decoder bcd_to_7_segment_decoder_10: pin names not known
  Register PC (.D(multiplexer_5_out), .en(CLK), .clk(CLK), .Q(out_1), .clr(Reiniciar));
  // _7_Segment_Display 7_segment_display_11: pin names not known; wires that end beside it: n7_segment_display_10_p4, n7_segment_display_11_p2
  _7_Segment_Display u_7_segment_display_12 ();  // open: g, f, a, b, e, d, c, dp
  // BCD_to_7_Segment_decoder bcd_to_7_segment_decoder_11: pin names not known
  // BCD_to_7_Segment_decoder bcd_to_7_segment_decoder_12: pin names not known
  Sumador sumador_1 (.A(8'h1), .B(out_1), .Cout(sumador_1_cout), .S(sumador_1_s));
  _7_Segment_Display u_7_segment_display_13 ();  // open: g, f, a, b, e, d, c, dp
  // BCD_to_7_Segment_decoder bcd_to_7_segment_decoder_13: pin names not known
  // Binary_to_BCD_converter #(.binvalue(8)) binary_to_bcd_converter_2: pin names not known; wires that end beside it: out_1
  ROM #(.dataWidth(16)) rom_1 (.addr(out_1), .data(rom_1_data));
  _7_Segment_Display u_7_segment_display_14 ();  // open: g, f, a, b, e, d, c, dp
  // BCD_to_7_Segment_decoder bcd_to_7_segment_decoder_14: pin names not known
  LED Reiniciado (.in(Reiniciar));
  // Binary_to_BCD_converter #(.binvalue(8)) binary_to_bcd_converter_3: pin names not known; wires that end beside it: binary_to_bcd_converter_3_p1, n7_segment_display_1_p1, n7_segment_display_1_p2, n7_segment_display_2_p2
  // Binary_to_BCD_converter #(.binvalue(8)) binary_to_bcd_converter_4: pin names not known; wires that end beside it: binary_to_bcd_converter_4_p1, n7_segment_display_5_p2, n7_segment_display_5_p3, n7_segment_display_7_p2
  // Binary_to_BCD_converter #(.binvalue(8)) binary_to_bcd_converter_5: pin names not known; wires that end beside it: binary_to_bcd_converter_5_p1, n7_segment_display_10_p3, n7_segment_display_10_p4, n7_segment_display_11_p2
  _7_Segment_Display u_7_segment_display_15 ();  // open: g, f, a, b, e, d, c, dp
  // BCD_to_7_Segment_decoder bcd_to_7_segment_decoder_15: pin names not known
  Button u_ReiniciarManual (.out(ReiniciarManual));
  Clock Reloj (.out(CLK));
  Control control_1 (
    .OPCODE(rom_1_data[15:14]), .Jump(control_1_jump), .ALUOP1(control_1_aluop0[1]),
    .ALUOP0(control_1_aluop0[0]), .RegDst(control_1_regdst), .ALUSrc(control_1_alusrc),
    .MemToReg(control_1_memtoreg), .RegWrite(control_1_regwrite), .MemRead(control_1_memread),
    .MemWrite(control_1_memwrite), .Branch(control_1_branch));
  and and_1 (and_1_out, control_1_jump, rom_1_data[13], rom_1_data[12], rom_1_data[11], rom_1_data[10], rom_1_data[9], rom_1_data[8]);
  or or_1 (Reiniciar, and_1_out, ReiniciarManual);
  Multiplexer #(.width(3)) multiplexer_1 (
    .in0(rom_1_data[10:8]), .in1(rom_1_data[7:5]), .out(multiplexer_1_out), .sel(control_1_regdst));
  Multiplexer multiplexer_2 (.in0(control_1_jump), .in1(1'b0), .out(multiplexer_2_out), .sel(and_1_out));
  ArchivoDeRegistros archivoderegistros_1 (
    .readRegister1(rom_1_data[13:11]), .readRegister2(rom_1_data[10:8]), .writeRegister(multiplexer_1_out),
    .writeData(multiplexer_6_out), .regWrite(control_1_regwrite), .Reiniciar(Reiniciar), .CLK(CLK),
    .A(binary_to_bcd_converter_3_p1), .B(binary_to_bcd_converter_4_p1), .C(binary_to_bcd_converter_5_p1),
    .readData1(archivoderegistros_1_readdata1), .readData2(archivoderegistros_1_readdata2));
  ALUControl alucontrol_1 (.FUNCT(rom_1_data[1:0]), .ALUOP(control_1_aluop0), .C(alucontrol_1_c));
  ALUCPU alucpu_1 (
    .A(archivoderegistros_1_readdata1), .B(multiplexer_3_out), .C(alucontrol_1_c), .Zero(alucpu_1_zero),
    .S(alucpu_1_s));  // open: Cout
  Multiplexer #(.width(8)) multiplexer_3 (
    .in0(archivoderegistros_1_readdata2), .in1(rom_1_data[7:0]), .out(multiplexer_3_out),
    .sel(control_1_alusrc));
  Sumador sumador_2 (.A(sumador_1_s), .B(rom_1_data[7:0]), .S(sumador_2_s));  // open: Cout
  and and_2 (and_2_out, control_1_branch, alucpu_1_zero);
  Multiplexer #(.width(8)) multiplexer_4 (
    .in0(sumador_1_s), .in1(sumador_2_s), .out(multiplexer_4_out), .sel(and_2_out));
  RAM dataMemory (
    .addr(alucpu_1_s), .we(control_1_memwrite), .oe(control_1_memread), .clk(CLK),
    .din(archivoderegistros_1_readdata2), .dout(dataMemory_dout));
  Multiplexer #(.width(8)) multiplexer_5 (
    .in0(multiplexer_4_out), .in1(rom_1_data[7:0]), .out(multiplexer_5_out), .sel(multiplexer_2_out));
  Multiplexer #(.width(8)) multiplexer_6 (
    .in0(alucpu_1_s), .in1(dataMemory_dout), .out(multiplexer_6_out), .sel(control_1_memtoreg));
  // also tied to GND on the sheet: sumador_1_cout

  // Notes on the sheet:
  //   A
  //   PC
  //   B
  //   +1
  //   C
  //   ADD-PC
  //   contents of rom_1 (hex, n*v repeats v):
  //   c900 d201 db00 e4e9 5c04 a62 1022 1842 8004 bf00
  //   Reinicia si se envia la señal 0xBF00
endmodule

module ALUControl (
  input  [1:0] FUNCT,
  input  [1:0] ALUOP,
  output [1:0] C
);

  wire and_1_out, and_2_out;

  and and_1 (and_1_out, FUNCT[1], ALUOP[1]);
  or or_1 (C[0], ALUOP[0], and_2_out);
  and and_2 (and_2_out, ALUOP[1], FUNCT[0]);
  or or_2 (C[1], ALUOP[0], and_1_out);
endmodule

module ALUCPU (
  input  [7:0] A,
  input  [1:0] C,
  input  [7:0] B,
  output Cout,
  output [7:0] S,
  output Zero
);

  wire [3:0] compand_1_s, compand_1_s_2, compand_1_s_3, compand_1_s_4, compand_1_s_5, compand_1_s_6,
       compand_1_s_7, compand_1_s_8;
  wire [3:2] sumador_1_cout;

  CompAND compand_1 (
    .A(A), .B(B),
    .S({compand_1_s_8[0], compand_1_s_7[0], compand_1_s_6[0], compand_1_s_5[0], compand_1_s_4[0], compand_1_s_3[0], compand_1_s_2[0], compand_1_s[0]}));
  CompOR compor_1 (
    .A(A), .B(B),
    .S({compand_1_s_8[1], compand_1_s_7[1], compand_1_s_6[1], compand_1_s_5[1], compand_1_s_4[1], compand_1_s_3[1], compand_1_s_2[1], compand_1_s[1]}));
  Sumador sumador_1 (
    .A(A), .B(B), .Cout(sumador_1_cout[2]),
    .S({compand_1_s_8[2], compand_1_s_7[2], compand_1_s_6[2], compand_1_s_5[2], compand_1_s_4[2], compand_1_s_3[2], compand_1_s_2[2], compand_1_s[2]}));
  Restador restador_1 (
    .A(A), .B(B), .Cout(sumador_1_cout[3]),
    .S({compand_1_s_8[3], compand_1_s_7[3], compand_1_s_6[3], compand_1_s_5[3], compand_1_s_4[3], compand_1_s_3[3], compand_1_s_2[3], compand_1_s[3]}));
  ExactlyOne xor_1 (
    .out(Zero), .in0(S[0]), .in1(S[1]), .in2(S[2]), .in3(S[3]), .in4(1'b1), .in5(S[4]), .in6(S[5]),
    .in7(S[6]), .in8(S[7]));
  SelectorMUX4 selectormux4_1 (.C(C), .E({sumador_1_cout, 2'b00}), .S(Cout));
  SelectorMUX4 selectormux4_2 (.C(C), .E(compand_1_s), .S(S[0]));
  SelectorMUX4 selectormux4_3 (.C(C), .E(compand_1_s_2), .S(S[1]));
  SelectorMUX4 selectormux4_4 (.C(C), .E(compand_1_s_3), .S(S[2]));
  SelectorMUX4 selectormux4_5 (.C(C), .E(compand_1_s_4), .S(S[3]));
  SelectorMUX4 selectormux4_6 (.C(C), .E(compand_1_s_5), .S(S[4]));
  SelectorMUX4 selectormux4_7 (.C(C), .E(compand_1_s_6), .S(S[5]));
  SelectorMUX4 selectormux4_8 (.C(C), .E(compand_1_s_7), .S(S[6]));
  SelectorMUX4 selectormux4_9 (.C(C), .E(compand_1_s_8), .S(S[7]));

  // Notes on the sheet:
  //   ZONA DE PRUEBA
  //   N
  //   0
  //   1
  //   2
  //   3
  //   00
  //   01
  //   10
  //   11
  //   Operación
  //   AND
  //   OR
  //   SUMA
  //   RESTA
  //   Bin
  //   00
  //   01
  //   10
  //   11
endmodule

module ArchivoDeRegistros (
  input  [2:0] readRegister1,
  input  [2:0] readRegister2,
  input  [2:0] writeRegister,
  input  [7:0] writeData,
  input  regWrite,
  input  Reiniciar,
  input  CLK,
  output [7:0] A,
  output [7:0] B,
  output [7:0] C,
  output [7:0] readData1,
  output [7:0] readData2
);

  wire and_1_out, and_2_out, and_3_out, and_4_out, and_5_out, decoder_1_out0, decoder_1_out1, decoder_1_out2,
       decoder_1_out3, decoder_1_out4;
  wire [7:0] RegD_q, ZERO_q;

  Decoder #(.enable("false"), .select(3)) decoder_1 (
    .out0(decoder_1_out0), .out1(decoder_1_out1), .out2(decoder_1_out2), .out3(decoder_1_out3),
    .out4(decoder_1_out4), .sel(writeRegister));  // open: out5, out6, out7
  and and_1 (and_1_out, decoder_1_out0, 1'b0, regWrite);
  and and_2 (and_2_out, decoder_1_out1, regWrite);
  and and_3 (and_3_out, decoder_1_out2, regWrite);
  and and_4 (and_4_out, decoder_1_out3, regWrite);
  and and_5 (and_5_out, decoder_1_out4, regWrite);
  Register ZERO (.D(writeData), .en(and_1_out), .clk(CLK), .Q(ZERO_q), .clr(Reiniciar));
  Register RegA (.D(writeData), .en(and_2_out), .clk(CLK), .Q(A), .clr(Reiniciar));
  Register RegB (.D(writeData), .en(and_3_out), .clk(CLK), .Q(B), .clr(Reiniciar));
  Register RegC (.D(writeData), .en(and_4_out), .clk(CLK), .Q(C), .clr(Reiniciar));
  Register RegD (.D(writeData), .en(and_5_out), .clk(CLK), .Q(RegD_q), .clr(Reiniciar));
  Multiplexer #(.select(3), .width(8)) multiplexer_1 (
    .in0(ZERO_q), .in1(A), .in2(B), .in3(C), .in4(RegD_q), .out(readData1), .sel(readRegister1));  // open: in5, in6, in7
  Multiplexer #(.select(3), .width(8)) multiplexer_2 (
    .in0(ZERO_q), .in1(A), .in2(B), .in3(C), .in4(RegD_q), .out(readData2), .sel(readRegister2));  // open: in5, in6, in7
endmodule

module Control (
  input  [1:0] OPCODE,
  output RegDst,
  output ALUSrc,
  output MemToReg,
  output RegWrite,
  output MemRead,
  output MemWrite,
  output Branch,
  output Jump,
  output ALUOP1,
  output ALUOP0
);

  wire not_1_out, not_2_out, not_3_out, not_4_out;

  not not_1 (not_1_out, OPCODE[1]);
  and TipoR (RegDst, not_1_out, not_2_out);
  not not_2 (not_2_out, OPCODE[0]);
  not not_3 (not_3_out, OPCODE[1]);
  and BEQ (ALUOP0, not_3_out, OPCODE[0]);
  not not_4 (not_4_out, OPCODE[0]);
  and J (Jump, OPCODE[1], not_4_out);
  and ADDI (ALUSrc, OPCODE[1], OPCODE[0]);
  or or_1 (RegWrite, RegDst, ALUSrc);
  or or_2 (ALUOP1, RegDst, ALUSrc);

  assign Branch = ALUOP0;
  assign MemRead = 1'b0;
  assign MemToReg = 1'b0;
  assign MemWrite = ALUSrc;
endmodule

module SelectorMUX4 (
  input  [1:0] C,
  input  [3:0] E,
  output S
);

  wire and_1_out, and_2_out, and_3_out, and_4_out, not_1_out, not_2_out;

  not not_1 (not_1_out, C[1]);
  not not_2 (not_2_out, C[0]);
  and and_1 (and_1_out, E[0], not_2_out, not_1_out);
  and and_2 (and_2_out, E[1], C[0], not_1_out);
  and and_3 (and_3_out, E[2], not_2_out, C[1]);
  and and_4 (and_4_out, E[3], C[0], C[1]);
  or or_1 (S, and_1_out, and_2_out, and_3_out, and_4_out);
endmodule

module SelectorMUX16 (
  input  [3:0] in_1,
  input  [15:0] in_2,
  output S
);

  wire and_1_out, and_2_out, and_3_out, and_4_out, and_5_out, and_6_out, and_7_out, and_8_out, and_9_out,
       and_10_out, and_11_out, and_12_out, and_13_out, and_14_out, and_15_out, and_16_out, not_1_out,
       not_2_out, not_3_out, not_4_out;

  not not_1 (not_1_out, in_1[3]);
  not not_2 (not_2_out, in_1[2]);
  not not_3 (not_3_out, in_1[1]);
  not not_4 (not_4_out, in_1[0]);
  and and_1 (and_1_out, in_2[0], not_4_out, not_3_out, not_2_out, not_1_out);
  and and_2 (and_2_out, in_2[1], in_1[0], not_3_out, not_2_out, not_1_out);
  and and_3 (and_3_out, in_2[2], not_4_out, in_1[1], not_2_out, not_1_out);
  and and_4 (and_4_out, in_2[3], in_1[0], in_1[1], not_2_out, not_1_out);
  and and_5 (and_5_out, in_2[4], not_4_out, not_3_out, in_1[2], not_1_out);
  and and_6 (and_6_out, in_2[5], in_1[0], not_3_out, in_1[2], not_1_out);
  and and_7 (and_7_out, in_2[6], not_4_out, in_1[1], in_1[2], not_1_out);
  and and_8 (and_8_out, in_2[7], in_1[0], in_1[1], in_1[2], not_1_out);
  and and_9 (and_9_out, in_2[8], not_4_out, not_3_out, not_2_out, in_1[3]);
  and and_10 (and_10_out, in_2[9], in_1[0], not_3_out, not_2_out, in_1[3]);
  and and_11 (and_11_out, in_2[10], not_4_out, in_1[1], not_2_out, in_1[3]);
  and and_12 (and_12_out, in_2[11], in_1[0], in_1[1], not_2_out, in_1[3]);
  and and_13 (and_13_out, in_2[12], not_4_out, not_3_out, in_1[2], in_1[3]);
  and and_14 (and_14_out, in_2[13], in_1[0], not_3_out, in_1[2], in_1[3]);
  and and_15 (and_15_out, in_2[14], not_4_out, in_1[1], in_1[2], in_1[3]);
  and and_16 (and_16_out, in_2[15], in_1[0], in_1[1], in_1[2], in_1[3]);
  or or_1 (S, and_1_out, and_2_out, and_3_out, and_4_out, and_5_out, and_6_out, and_7_out, and_8_out, and_9_out, and_10_out, and_11_out, and_12_out, and_13_out, and_14_out, and_15_out, and_16_out);
endmodule

module ALU (
  input  [7:0] A,
  input  [3:0] C,
  input  [7:0] B,
  output Zero,
  output Cout,
  output [7:0] S
);

  wire [1:0] sumador_1_cout;
  wire [4:0] compand_1_s, compnand_1_s, compnor_1_s, compor_1_s, compxnor_1_s, compxor_1_s, restador_1_s,
       sumador_1_s;
  wire [7:0] sumador_1_s_2, sumador_1_s_3, sumador_1_s_4;

  Sumador sumador_1 (
    .A(A), .B(B), .Cout(sumador_1_cout[0]),
    .S({sumador_1_s_4[0], sumador_1_s_3[0], sumador_1_s_2[0], sumador_1_s}));
  Restador restador_1 (
    .A(A), .B(B), .Cout(sumador_1_cout[1]),
    .S({sumador_1_s_4[1], sumador_1_s_3[1], sumador_1_s_2[1], restador_1_s}));
  CompOR compor_1 (.A(A), .B(B), .S({sumador_1_s_4[2], sumador_1_s_3[2], sumador_1_s_2[2], compor_1_s}));
  CompAND compand_1 (.A(A), .B(B), .S({sumador_1_s_4[3], sumador_1_s_3[3], sumador_1_s_2[3], compand_1_s}));
  CompXOR compxor_1 (.A(A), .B(B), .S({sumador_1_s_4[4], sumador_1_s_3[4], sumador_1_s_2[4], compxor_1_s}));
  CompNAND compnand_1 (.A(A), .B(B), .S({sumador_1_s_4[5], sumador_1_s_3[5], sumador_1_s_2[5], compnand_1_s}));
  CompNOR compnor_1 (.A(A), .B(B), .S({sumador_1_s_4[6], sumador_1_s_3[6], sumador_1_s_2[6], compnor_1_s}));
  CompXNOR compxnor_1 (.A(A), .B(B), .S({sumador_1_s_4[7], sumador_1_s_3[7], sumador_1_s_2[7], compxnor_1_s}));
  SelectorMUX16 selectormux16_1 (.in_1(C), .in_2({{14{1'b0}}, sumador_1_cout}), .S(Cout));
  SelectorMUX16 selectormux16_2 (
    .in_1(C),
    .in_2({{8{1'b0}}, compxnor_1_s[0], compnor_1_s[0], compnand_1_s[0], compxor_1_s[0], compand_1_s[0], compor_1_s[0], restador_1_s[0], sumador_1_s[0]}),
    .S(S[0]));
  SelectorMUX16 selectormux16_3 (
    .in_1(C),
    .in_2({{8{1'b0}}, compxnor_1_s[1], compnor_1_s[1], compnand_1_s[1], compxor_1_s[1], compand_1_s[1], compor_1_s[1], restador_1_s[1], sumador_1_s[1]}),
    .S(S[1]));
  SelectorMUX16 selectormux16_4 (
    .in_1(C),
    .in_2({{8{1'b0}}, compxnor_1_s[2], compnor_1_s[2], compnand_1_s[2], compxor_1_s[2], compand_1_s[2], compor_1_s[2], restador_1_s[2], sumador_1_s[2]}),
    .S(S[2]));
  SelectorMUX16 selectormux16_5 (
    .in_1(C),
    .in_2({{8{1'b0}}, compxnor_1_s[3], compnor_1_s[3], compnand_1_s[3], compxor_1_s[3], compand_1_s[3], compor_1_s[3], restador_1_s[3], sumador_1_s[3]}),
    .S(S[3]));
  ExactlyOne xor_1 (
    .out(Zero), .in0(S[0]), .in1(S[1]), .in2(S[2]), .in3(S[3]), .in4(1'b1), .in5(S[4]), .in6(S[5]),
    .in7(S[6]), .in8(S[7]));
  SelectorMUX16 selectormux16_6 (
    .in_1(C),
    .in_2({{8{1'b0}}, compxnor_1_s[4], compnor_1_s[4], compnand_1_s[4], compxor_1_s[4], compand_1_s[4], compor_1_s[4], restador_1_s[4], sumador_1_s[4]}),
    .S(S[4]));
  SelectorMUX16 selectormux16_7 (.in_1(C), .in_2({{8{1'b0}}, sumador_1_s_2}), .S(S[5]));
  SelectorMUX16 selectormux16_8 (.in_1(C), .in_2({{8{1'b0}}, sumador_1_s_3}), .S(S[6]));
  SelectorMUX16 selectormux16_9 (.in_1(C), .in_2({{8{1'b0}}, sumador_1_s_4}), .S(S[7]));

  // Notes on the sheet:
  //   ZONA DE PRUEBA
  //   N
  //   Operación
  //   0   Sumar
  //   1   Restar
  //   2   OR
  //   3   AND
  //   4   XOR
  //   5   NAND
  //   6   NOR
  //   7   XNOR
  //   ESTA ALU ESTA MAS COMPLETA, EL CPU USA UNA VERSIÓN SIMPLIFICADA
  //   Bin
  //   000
  //   001
  //   010
  //   011
  //   100
  //   101
  //   110
  //   111
endmodule

module FullAdderCasero (
  input  A,
  input  B,
  input  Cin,
  output S,
  output Cout
);

  wire and_1_out, and_2_out, xor_1_out;

  xor xor_1 (xor_1_out, A, B);
  Adder adder_1 ();  // open: a, b, out, cin, cout
  xor xor_2 (S, xor_1_out, Cin);
  and and_1 (and_1_out, Cin, xor_1_out);
  and and_2 (and_2_out, B, A);
  or or_1 (Cout, and_1_out, and_2_out);

  // Notes on the sheet:
  //   Full Adder Casero
endmodule

module Sumador (
  input  [7:0] A,
  input  [7:0] B,
  output Cout,
  output [7:0] S
);

  wire fulladdercasero_2_cout, fulladdercasero_3_cout, fulladdercasero_4_cout, fulladdercasero_5_cout,
       fulladdercasero_6_cout, fulladdercasero_7_cout, fulladdercasero_8_cout;

  FullAdderCasero fulladdercasero_1 (.A(A[7]), .B(B[7]), .Cin(fulladdercasero_2_cout), .S(S[7]), .Cout(Cout));
  FullAdderCasero fulladdercasero_2 (
    .A(A[6]), .B(B[6]), .Cin(fulladdercasero_3_cout), .S(S[6]), .Cout(fulladdercasero_2_cout));
  FullAdderCasero fulladdercasero_3 (
    .A(A[5]), .B(B[5]), .Cin(fulladdercasero_4_cout), .S(S[5]), .Cout(fulladdercasero_3_cout));
  FullAdderCasero fulladdercasero_4 (
    .A(A[4]), .B(B[4]), .Cin(fulladdercasero_5_cout), .S(S[4]), .Cout(fulladdercasero_4_cout));
  FullAdderCasero fulladdercasero_5 (
    .A(A[3]), .B(B[3]), .Cin(fulladdercasero_6_cout), .S(S[3]), .Cout(fulladdercasero_5_cout));
  FullAdderCasero fulladdercasero_6 (
    .A(A[2]), .B(B[2]), .Cin(fulladdercasero_7_cout), .S(S[2]), .Cout(fulladdercasero_6_cout));
  Adder adder_1 ();  // open: a, b, out, cin, cout
  FullAdderCasero fulladdercasero_7 (
    .A(A[1]), .B(B[1]), .Cin(fulladdercasero_8_cout), .S(S[1]), .Cout(fulladdercasero_7_cout));
  FullAdderCasero fulladdercasero_8 (.A(A[0]), .B(B[0]), .Cin(1'b0), .S(S[0]), .Cout(fulladdercasero_8_cout));

  // Notes on the sheet:
  //   +
  //   --------------------
  //   Sumador Casero
endmodule

module Restador (
  input  [7:0] A,
  input  [7:0] B,
  output Cout,
  output [7:0] S
);

  wire B0, B1, B2, B3, B4, B5, B6, B7, fulladdercasero_1_cout, fulladdercasero_2_cout,
       fulladdercasero_3_cout, fulladdercasero_4_cout, fulladdercasero_5_cout, fulladdercasero_6_cout,
       fulladdercasero_7_cout, fulladdercasero_8_cout;

  not not_1 (Cout, fulladdercasero_1_cout);
  FullAdderCasero fulladdercasero_1 (
    .A(A[7]), .B(B7), .Cin(fulladdercasero_2_cout), .S(S[7]), .Cout(fulladdercasero_1_cout));
  FullAdderCasero fulladdercasero_2 (
    .A(A[6]), .B(B6), .Cin(fulladdercasero_3_cout), .S(S[6]), .Cout(fulladdercasero_2_cout));
  FullAdderCasero fulladdercasero_3 (
    .A(A[5]), .B(B5), .Cin(fulladdercasero_4_cout), .S(S[5]), .Cout(fulladdercasero_3_cout));
  assign {B7, B6, B5, B4, B3, B2, B1, B0} = ~B;  // NOT_Gate not_2, 8 bits wide
  FullAdderCasero fulladdercasero_4 (
    .A(A[4]), .B(B4), .Cin(fulladdercasero_5_cout), .S(S[4]), .Cout(fulladdercasero_4_cout));
  FullAdderCasero fulladdercasero_5 (
    .A(A[3]), .B(B3), .Cin(fulladdercasero_6_cout), .S(S[3]), .Cout(fulladdercasero_5_cout));
  FullAdderCasero fulladdercasero_6 (
    .A(A[2]), .B(B2), .Cin(fulladdercasero_7_cout), .S(S[2]), .Cout(fulladdercasero_6_cout));
  Subtractor subtractor_1 ();  // open: a, b, out, bin, bout
  FullAdderCasero fulladdercasero_7 (
    .A(A[1]), .B(B1), .Cin(fulladdercasero_8_cout), .S(S[1]), .Cout(fulladdercasero_7_cout));
  FullAdderCasero fulladdercasero_8 (.A(A[0]), .B(B0), .Cin(1'b1), .S(S[0]), .Cout(fulladdercasero_8_cout));

  // Notes on the sheet:
  //   -
  //   --------------------
  //   Restador Casero
endmodule

module CompOR (
  input  [7:0] A,
  input  [7:0] B,
  output [7:0] S
);

  or or_1 (S[7], A[7], B[7]);
  or or_2 (S[6], A[6], B[6]);
  or or_3 (S[5], A[5], B[5]);
  or or_4 (S[4], A[4], B[4]);
  or or_5 (S[3], A[3], B[3]);
  or or_6 (S[2], A[2], B[2]);
  or or_7 (S[1], A[1], B[1]);
  or or_8 (S[0], A[0], B[0]);

  // Notes on the sheet:
  //   OR
  //   --------------------
endmodule

module CompAND (
  input  [7:0] A,
  input  [7:0] B,
  output [7:0] S
);

  and and_1 (S[7], A[7], B[7]);
  and and_2 (S[6], A[6], B[6]);
  and and_3 (S[5], A[5], B[5]);
  and and_4 (S[4], A[4], B[4]);
  and and_5 (S[3], A[3], B[3]);
  and and_6 (S[2], A[2], B[2]);
  and and_7 (S[1], A[1], B[1]);
  and and_8 (S[0], A[0], B[0]);

  // Notes on the sheet:
  //   AND
  //   --------------------
endmodule

module CompXOR (
  input  [7:0] A,
  input  [7:0] B,
  output [7:0] S
);

  xor xor_1 (S[7], A[7], B[7]);
  xor xor_2 (S[6], A[6], B[6]);
  xor xor_3 (S[5], A[5], B[5]);
  xor xor_4 (S[4], A[4], B[4]);
  xor xor_5 (S[3], A[3], B[3]);
  xor xor_6 (S[2], A[2], B[2]);
  xor xor_7 (S[1], A[1], B[1]);
  xor xor_8 (S[0], A[0], B[0]);

  // Notes on the sheet:
  //   XOR
  //   --------------------
endmodule

module CompNAND (
  input  [7:0] A,
  input  [7:0] B,
  output [7:0] S
);

  nand nand_1 (S[7], A[7], B[7]);
  nand nand_2 (S[6], A[6], B[6]);
  nand nand_3 (S[5], A[5], B[5]);
  nand nand_4 (S[4], A[4], B[4]);
  nand nand_5 (S[3], A[3], B[3]);
  nand nand_6 (S[2], A[2], B[2]);
  nand nand_7 (S[1], A[1], B[1]);
  nand nand_8 (S[0], A[0], B[0]);

  // Notes on the sheet:
  //   NAND
  //   --------------------
endmodule

module CompNOR (
  input  [7:0] A,
  input  [7:0] B,
  output [7:0] S
);

  nor nor_1 (S[7], A[7], B[7]);
  nor nor_2 (S[6], A[6], B[6]);
  nor nor_3 (S[5], A[5], B[5]);
  nor nor_4 (S[4], A[4], B[4]);
  nor nor_5 (S[3], A[3], B[3]);
  nor nor_6 (S[2], A[2], B[2]);
  nor nor_7 (S[1], A[1], B[1]);
  nor nor_8 (S[0], A[0], B[0]);

  // Notes on the sheet:
  //   NOR
  //   --------------------
endmodule

module CompXNOR (
  input  [7:0] A,
  input  [7:0] B,
  output [7:0] S
);

  xnor xnor_1 (S[7], A[7], B[7]);
  xnor xnor_2 (S[6], A[6], B[6]);
  xnor xnor_3 (S[5], A[5], B[5]);
  xnor xnor_4 (S[4], A[4], B[4]);
  xnor xnor_5 (S[3], A[3], B[3]);
  xnor xnor_6 (S[2], A[2], B[2]);
  xnor xnor_7 (S[1], A[1], B[1]);
  xnor xnor_8 (S[0], A[0], B[0]);

  // Notes on the sheet:
  //   XNOR
  //   --------------------
endmodule
